// Logisim project cpu.circ as structural Verilog: 1 circuit, main circuit main
module main (
  output [15:0] pc,
  output halt
);

  wire clock_1_out, clock_2_out, clock_3_out, clock_4_out, not_1_out, rom_1_sel;
  wire [7:0] A, B, ctl, imm, memaddr, memdata;
  wire [15:0] adder_1_out, bit_extender_1_out, multiplexer_1_out;

  // Probe on pc
  // Probe on ctl
  // Probe on imm
  Multiplexer #(.width(16)) multiplexer_1 (
    .in0(16'h1), .in1(bit_extender_1_out), .out(multiplexer_1_out), .sel(ctl[0]), .en(1'b1));
  assign bit_extender_1_out = {{8{imm[7]}}, imm};  // Bit_Extender bit_extender_1
  // Probe on memaddr
  // Probe on memdata
  Adder #(.width(16)) adder_1 (.a(pc), .b(multiplexer_1_out), .out(adder_1_out));  // open: cin, cout
  // Probe on A
  // Probe on B
  Register #(.width(16)) u_PC (.D(adder_1_out), .Q(pc), .clk(clock_1_out));  // open: en, clr
  Clock clock_1 (.out(clock_1_out));
  rom rom_1 (.A(pc), .sel(rom_1_sel), .D({imm, ctl}));
  Comparator #(.width(16), .mode("unsigned")) comparator_1 (.a({imm, ctl}), .b(16'h1), .eq(halt));  // open: gt, lt
  // Probe on {imm, ctl}
  Multiplexer #(.select(2), .width(8)) multiplexer_2 (
    .in0(A), .in1(B), .in2(imm), .in3(imm), .out(memaddr), .sel({ctl[3], ctl[4]}), .en(1'b1));
  not not_1 (not_1_out, ctl[2]);
  Clock clock_2 (.out(clock_2_out));
  RAM #(.bus("asynch")) ram_1 (.addr(memaddr), .data(memdata), .sel(1'b1), .ld(not_1_out));  // open: clr
  Register register_1 (.D(memdata), .en(ctl[5]), .Q(A), .clk(clock_3_out));  // open: clr
  Clock clock_3 (.out(clock_3_out));
  Register register_2 (.D(memdata), .en(ctl[6]), .Q(B), .clk(clock_4_out));  // open: clr
  Clock clock_4 (.out(clock_4_out));
  // also tied to VCC on the sheet: rom_1_sel

  // Other names for the same wires on the sheet: ctrl_memaddrrb = ctl[4]; insn[15:0] = {imm, ctl};
  //   ctrl_memaddrimm = ctl[3]; ctl_jmp = ctl[0]; ctrl_memwr = ctl[2]; ctrl_dstra = ctl[5]; ctrl_dstrb = ctl[6]
endmodule
